// Digital circuit 5bitPC2.dig as structural Verilog
module _5bitPC2 (
  input  Re_a,
  input  Le_a,
  input  CNTe_a,
  input  CLK,
  input  CLR,
  input  [7:0] PC_in,
  output [5:0] PC_out
);

  wire and_1_out, and_2_out, and_3_out, and_4_out, and_5_out, and_6_out, and_7_out, and_8_out, and_9_out,
       and_10_out, and_11_out, and_12_out, and_13_out, and_14_out, and_15_out, and_16_out, and_17_out,
       not_1_out, not_2_out, not_3_out, not_4_out, not_5_out, not_6_out, or_1_out, or_2_out, or_3_out,
       or_4_out, or_5_out, or_6_out;
  wire [5:0] A0_d;

  and and_1 (and_1_out, PC_in[0], Le_a);
  not not_1 (not_1_out, and_1_out);
  and and_2 (and_2_out, not_1_out, Le_a);
  or or_1 (or_1_out, and_2_out, CLR);
  JK_FF_AS jk_ff_as_1 (.Set(and_1_out), .J(CNTe_a), .C(CLK), .K(CNTe_a), .Clr(or_1_out), .Q(A0_d[0]));  // open: nQ
  and and_3 (and_3_out, PC_in[1], Le_a);
  and and_4 (and_4_out, CNTe_a, A0_d[0]);
  assign PC_out[0] = Re_a ? A0_d[0] : 1'bz;  // Driver driver_1
  not not_2 (not_2_out, and_3_out);
  and and_5 (and_5_out, not_2_out, Le_a);
  assign PC_out[1] = Re_a ? A0_d[1] : 1'bz;  // Driver driver_2
  or or_2 (or_2_out, and_5_out, CLR);
  assign PC_out[2] = Re_a ? A0_d[2] : 1'bz;  // Driver driver_3
  JK_FF_AS jk_ff_as_2 (
    .Set(and_3_out), .J(and_4_out), .C(CLK), .K(and_4_out), .Clr(or_2_out), .Q(A0_d[1]));  // open: nQ
  and and_6 (and_6_out, PC_in[2], Le_a);
  and and_7 (and_7_out, CNTe_a, and_4_out, A0_d[1]);
  assign PC_out[3] = Re_a ? A0_d[3] : 1'bz;  // Driver driver_4
  assign PC_out[4] = Re_a ? A0_d[4] : 1'bz;  // Driver driver_5
  not not_3 (not_3_out, and_6_out);
  and and_8 (and_8_out, not_3_out, Le_a);
  or or_3 (or_3_out, and_8_out, CLR);
  assign PC_out[5] = Re_a ? A0_d[5] : 1'bz;  // Driver driver_6
  JK_FF_AS jk_ff_as_3 (
    .Set(and_6_out), .J(and_7_out), .C(CLK), .K(and_7_out), .Clr(or_3_out), .Q(A0_d[2]));  // open: nQ
  and and_9 (and_9_out, PC_in[3], Le_a);
  and and_10 (and_10_out, CNTe_a, and_7_out, A0_d[2]);
  not not_4 (not_4_out, and_9_out);
  and and_11 (and_11_out, not_4_out, Le_a);
  or or_4 (or_4_out, and_11_out, CLR);
  JK_FF_AS jk_ff_as_4 (
    .Set(and_9_out), .J(and_10_out), .C(CLK), .K(and_10_out), .Clr(or_4_out), .Q(A0_d[3]));  // open: nQ
  and and_12 (and_12_out, CNTe_a, and_10_out, A0_d[3]);
  and and_13 (and_13_out, PC_in[4], Le_a);
  not not_5 (not_5_out, and_13_out);
  and and_14 (and_14_out, not_5_out, Le_a);
  or or_5 (or_5_out, and_14_out, CLR);
  JK_FF_AS jk_ff_as_5 (
    .Set(and_13_out), .J(and_12_out), .C(CLK), .K(and_12_out), .Clr(or_5_out), .Q(A0_d[4]));  // open: nQ
  and and_15 (and_15_out, CNTe_a, and_12_out, A0_d[4]);
  and and_16 (and_16_out, PC_in[5], Le_a);
  not not_6 (not_6_out, and_16_out);
  and and_17 (and_17_out, not_6_out, Le_a);
  or or_6 (or_6_out, and_17_out, CLR);
  JK_FF_AS jk_ff_as_6 (
    .Set(and_16_out), .J(and_15_out), .C(CLK), .K(and_15_out), .Clr(or_6_out), .Q(A0_d[5]));  // open: nQ
endmodule

/* Test case TesteBasico:
CLK CNTe_a CLR Le_a Re_a   PC_in PC_out 
loop(A,8)
let Bi = random(32);
0    0     0    1    1    (Bi)    (Bi)	
C    0     0    1    1    (Bi)    (Bi)	
end loop
C    0     1    0    1     X      0
loop(A,4)
let Bi = random(32);
C    1     0    0    1   (Bi)  (A+1)	
end loop
let Bi = random(32);
0    0     0    1    1    (Bi)    (Bi)	
loop(A,6)
C    1     0    0    1   0  (A+1+Bi)	
end loop
*/
