// Digital circuit 5bitPc0.dig as structural Verilog
module _5bitPc0 (
  input  Re_a,
  input  Le_a,
  input  CNTe_a,
  input  CLK,
  input  CLR,
  output AI0,
  output AI1,
  output AI2,
  output AI3
);

  wire and_1_out, and_2_out, and_3_out, and_4_out, and_5_out, and_6_out, and_7_out, and_8_out, and_9_out,
       jk_ff_as_1_q, jk_ff_as_2_q, jk_ff_as_3_q, jk_ff_as_4_q, jk_ff_as_5_q;
  wire [3:0] pullup_1_out;

  buf and_1 (and_1_out, Le_a);  // And open: In_1
  buf and_2 (and_2_out, Le_a);  // And open: In_1
  and and_3 (and_3_out, CNTe_a, jk_ff_as_1_q);
  JK_FF_AS jk_ff_as_1 (.Set(and_1_out), .J(CNTe_a), .C(CLK), .K(CNTe_a), .Clr(CLR), .Q(jk_ff_as_1_q));  // open: nQ
  assign AI0 = Re_a ? jk_ff_as_1_q : 1'bz;  // Driver driver_1
  buf and_4 (and_4_out, Le_a);  // And open: In_1
  and and_5 (and_5_out, CNTe_a, and_3_out, jk_ff_as_2_q);
  JK_FF_AS jk_ff_as_2 (
    .Set(and_2_out), .J(and_3_out), .C(CLK), .K(and_3_out), .Clr(CLR), .Q(jk_ff_as_2_q));  // open: nQ
  assign AI1 = Re_a ? jk_ff_as_2_q : 1'bz;  // Driver driver_2
  buf and_6 (and_6_out, Le_a);  // And open: In_1
  and and_7 (and_7_out, CNTe_a, and_5_out, jk_ff_as_3_q);
  JK_FF_AS jk_ff_as_3 (
    .Set(and_4_out), .J(and_5_out), .C(CLK), .K(and_5_out), .Clr(CLR), .Q(jk_ff_as_3_q));  // open: nQ
  assign AI2 = Re_a ? jk_ff_as_3_q : 1'bz;  // Driver driver_3
  buf and_8 (and_8_out, Le_a);  // And open: In_1
  and and_9 (and_9_out, CNTe_a, and_7_out, jk_ff_as_4_q);
  JK_FF_AS jk_ff_as_4 (
    .Set(and_6_out), .J(and_7_out), .C(CLK), .K(and_7_out), .Clr(CLR), .Q(jk_ff_as_4_q));  // open: nQ
  assign AI3 = Re_a ? jk_ff_as_4_q : 1'bz;  // Driver driver_4
  JK_FF_AS jk_ff_as_5 (
    .Set(and_8_out), .J(and_9_out), .C(CLK), .K(and_9_out), .Clr(CLR), .Q(jk_ff_as_5_q));  // open: nQ
  PullUp #(.Bits(4)) pullup_1 (.out(pullup_1_out));
  Seven_Seg_Hex seven_seg_hex_1 ();  // open: d, dp
endmodule
