// Digital circuit 5bitPc1.dig as structural Verilog
module _5bitPc1 (
  input  Re_a,
  input  CLR,
  input  clk,
  input  D0_a,
  input  CCNT_e,
  input  D1_a,
  input  ncnt__LD,
  input  KSCD,
  output AI0,
  output AI1,
  output AI2,
  output AI3
);

  wire and_1_out, and_2_out, and_3_out, and_4_out, and_5_out, and_6_out, jk_ff_as_1_q, jk_ff_as_2_q,
       not_1_out, not_2_out, not_3_out, not_4_out, or_1_out, or_2_out;
  wire [3:0] pullup_2_out, pullup_5_out;

  not not_1 (not_1_out, D0_a);
  not not_2 (not_2_out, ncnt__LD);
  and and_1 (and_1_out, not_1_out, ncnt__LD);
  and and_2 (and_2_out, D0_a, ncnt__LD);
  and and_3 (and_3_out, CCNT_e, KSCD, not_2_out);
  or or_1 (or_1_out, and_1_out, CLR);
  JK_FF_AS jk_ff_as_1 (
    .Set(and_2_out), .J(and_3_out), .C(clk), .K(and_3_out), .Clr(or_1_out), .Q(jk_ff_as_1_q));  // open: nQ
  LED led_1 (.in(jk_ff_as_1_q));
  not not_3 (not_3_out, D1_a);
  PullUp pullup_1 (.out(pullup_2_out[0]));
  assign AI0 = Re_a ? pullup_2_out[0] : 1'bz;  // Driver driver_1
  not not_4 (not_4_out, ncnt__LD);
  and and_4 (and_4_out, not_3_out, ncnt__LD);
  and and_5 (and_5_out, D1_a, ncnt__LD);
  or or_2 (or_2_out, and_4_out, CLR);
  PullUp pullup_2 (.out(pullup_2_out[1]));
  assign AI1 = Re_a ? pullup_2_out[1] : 1'bz;  // Driver driver_2
  and and_6 (and_6_out, CCNT_e, jk_ff_as_1_q, not_4_out);
  PullUp pullup_3 (.out(pullup_2_out[2]));
  assign AI2 = Re_a ? pullup_2_out[2] : 1'bz;  // Driver driver_3
  JK_FF_AS jk_ff_as_2 (
    .Set(and_5_out), .J(and_6_out), .C(clk), .K(and_6_out), .Clr(or_2_out), .Q(jk_ff_as_2_q));  // open: nQ
  LED led_2 (.in(jk_ff_as_2_q));
  PullUp pullup_4 (.out(pullup_2_out[3]));
  assign AI3 = Re_a ? pullup_2_out[3] : 1'bz;  // Driver driver_4
  Seven_Seg_Hex seven_seg_hex_1 (.d(pullup_2_out), .dp(1'b0));
  PullUp #(.Bits(4)) pullup_5 (.out(pullup_5_out));

  // Notes on the sheet:
  //   CCNT_e: default 1
  //   KSCD: default 1
endmodule
