// Digital circuit DffwEna.dig as structural Verilog
module DffwEna (
  input  D,
  input  E_out,
  input  E_in,
  output Q
);

  wire nand_1_out, nand_2_out, nand_3_out, nand_4_out, not_1_out;

  not not_1 (not_1_out, D);
  nand nand_1 (nand_1_out, D, E_in);
  nand nand_2 (nand_2_out, not_1_out, E_in);
  nand nand_3 (nand_3_out, nand_1_out, nand_4_out);
  nand nand_4 (nand_4_out, nand_3_out, nand_2_out);
  assign Q = E_out ? nand_3_out : 1'bz;  // Driver driver_1
endmodule
