// Digital circuit Sap1PC5bits.dig as structural Verilog
module Sap1PC5bits (
  input  clk,
  input  ncnt_LD,
  input  CLR,
  input  CNT_E,
  input  in_5,
  input  in_6,
  input  in_7,
  input  in_8,
  input  in_9,
  input  in_10
);

  wire and_1_out, and_2_out, and_3_out, dipswitch_1_out, ldpc0_bit_1_q, ldpc0_bit_2_q, ldpc0_bit_3_q,
       ldpc0_bit_4_q, ldpc0_bit_5_q;
  wire [1:0] counter_1_out;

  DipSwitch dipswitch_1 (.out(dipswitch_1_out));
  Counter #(.Bits(2), .isProgramCounter("true")) counter_1 (
    .en(in_9), .C(clk), .clr(dipswitch_1_out), .out(counter_1_out));  // open: ovf
  LED led_1 (.in(counter_1_out[0]));
  LED led_2 (.in(counter_1_out[1]));
  ldPC0_bit ldpc0_bit_1 (
    .CLR(CLR), .D0_a(in_5), .CCNT_e(CNT_E), .ncnt__LD(ncnt_LD), .KSCD(1'b1), .CLK(counter_1_out[1]),
    .Q(ldpc0_bit_1_q));  // open: nQ
  LED led_3 (.in(ldpc0_bit_1_q));
  ldPC0_bit ldpc0_bit_2 (
    .CLR(CLR), .D0_a(in_6), .CCNT_e(CNT_E), .ncnt__LD(ncnt_LD), .KSCD(ldpc0_bit_1_q), .CLK(counter_1_out[1]),
    .Q(ldpc0_bit_2_q));  // open: nQ
  and and_1 (and_1_out, ldpc0_bit_2_q, ldpc0_bit_1_q);
  LED led_4 (.in(ldpc0_bit_2_q));
  ldPC0_bit ldpc0_bit_3 (
    .CLR(CLR), .D0_a(in_7), .CCNT_e(CNT_E), .ncnt__LD(ncnt_LD), .KSCD(and_1_out), .CLK(counter_1_out[1]),
    .Q(ldpc0_bit_3_q));  // open: nQ
  and and_2 (and_2_out, ldpc0_bit_3_q, and_1_out);
  LED led_5 (.in(ldpc0_bit_3_q));
  ldPC0_bit ldpc0_bit_4 (
    .CLR(CLR), .D0_a(in_8), .CCNT_e(CNT_E), .ncnt__LD(ncnt_LD), .KSCD(and_2_out), .CLK(counter_1_out[1]),
    .Q(ldpc0_bit_4_q));  // open: nQ
  and and_3 (and_3_out, ldpc0_bit_4_q, and_2_out);
  LED led_6 (.in(ldpc0_bit_4_q));
  ldPC0_bit ldpc0_bit_5 (
    .CLR(CLR), .D0_a(in_10), .CCNT_e(CNT_E), .ncnt__LD(ncnt_LD), .KSCD(and_3_out), .CLK(counter_1_out[1]),
    .Q(ldpc0_bit_5_q));  // open: nQ
  LED led_7 (.in(ldpc0_bit_5_q));

  // Notes on the sheet:
  //   clk: Hz: 5
  //   in_9: default 1
endmodule
