// Digital circuit base0.dig as structural Verilog
module base0 (
);

  wire dipswitch_1_out, dipswitch_2_out, dipswitch_3_out, dipswitch_4_out, dipswitch_5_out, dipswitch_6_out,
       dipswitch_7_out, dipswitch_8_out, dipswitch_9_out, dipswitch_10_out;
  wire [3:0] reg0_1_q0, reg0_1_q4;

  DipSwitch dipswitch_1 (.out(dipswitch_1_out));
  DipSwitch dipswitch_2 (.out(dipswitch_2_out));
  DipSwitch dipswitch_3 (.out(dipswitch_3_out));
  DipSwitch dipswitch_4 (.out(dipswitch_4_out));
  DipSwitch dipswitch_5 (.out(dipswitch_5_out));
  DipSwitch dipswitch_6 (.out(dipswitch_6_out));
  DipSwitch dipswitch_7 (.out(dipswitch_7_out));
  DipSwitch dipswitch_8 (.out(dipswitch_8_out));
  DipSwitch dipswitch_9 (.out(dipswitch_9_out));
  DipSwitch dipswitch_10 (.out(dipswitch_10_out));
  reg0 reg0_1 (
    .D0(dipswitch_1_out), .ENA_i(dipswitch_9_out), .D1(dipswitch_2_out), .D2(dipswitch_3_out),
    .D3(dipswitch_4_out), .D4(dipswitch_5_out), .D5(dipswitch_6_out), .D6(dipswitch_7_out),
    .D7(dipswitch_8_out), .ENA_o(dipswitch_10_out), .Q0(reg0_1_q0[0]), .Q1(reg0_1_q0[1]), .Q2(reg0_1_q0[2]),
    .Q3(reg0_1_q0[3]), .Q4(reg0_1_q4[0]), .Q5(reg0_1_q4[1]), .Q6(reg0_1_q4[2]), .Q7(reg0_1_q4[3]));
  Seven_Seg_Hex seven_seg_hex_1 (.d(reg0_1_q0), .dp(1'b0));
  Seven_Seg_Hex seven_seg_hex_2 (.d(reg0_1_q4), .dp(1'b0));
endmodule
