// Digital circuit d01.dig as structural Verilog
module d01 (
  input  D,
  input  Ei,
  input  Eo,
  input  clk
);

  wire driver_1_out, driver_2_out, nand_1_out, nand_2_out, nand_3_out, nand_4_out, nand_5_out, nand_6_out,
       nand_7_out, nand_8_out, not_1_out, not_2_out;

  not not_1 (not_1_out, D);
  not not_2 (not_2_out, clk);
  nand nand_1 (nand_1_out, clk, D);
  nand nand_2 (nand_2_out, not_1_out, clk);
  nand nand_3 (nand_3_out, nand_1_out, nand_4_out);
  nand nand_4 (nand_4_out, nand_3_out, nand_2_out);
  nand nand_5 (nand_5_out, nand_3_out, not_2_out);
  nand nand_6 (nand_6_out, not_2_out, nand_4_out);
  nand nand_7 (nand_7_out, nand_8_out, nand_6_out);
  nand nand_8 (nand_8_out, nand_5_out, nand_7_out);
  LED S (.in(nand_8_out));
  LED R (.in(nand_7_out));
  assign driver_1_out = Eo ? nand_8_out : 1'bz;  // Driver driver_1
  assign driver_2_out = Eo ? nand_7_out : 1'bz;  // Driver driver_2
  LED S_2 (.in(driver_1_out));
  LED R_2 (.in(driver_2_out));
endmodule
