// Digital circuit jk0.dig as structural Verilog
module jk0 (
  input  Ei,
  input  clk,
  input  J0,
  input  K0
);

  wire nand_1_out, nand_2_out, nand_3_out, nand_4_out, nand_5_out, nand_6_out, nand_7_out, nand_8_out,
       nand_9_out, nand_10_out, nand_11_out, nand_12_out, nand_13_out, nand_14_out, nand_15_out, nand_16_out,
       nand_17_out, nand_18_out, nand_19_out, nand_20_out, nand_21_out, nand_22_out, nand_23_out,
       nand_24_out, not_1_out, not_2_out, not_3_out;

  nand nand_1 (nand_1_out, clk, nand_7_out, nand_24_out);
  nand nand_2 (nand_2_out, nand_23_out, nand_8_out, clk);
  not not_1 (not_1_out, clk);
  nand nand_3 (nand_3_out, nand_1_out, nand_4_out);
  nand nand_4 (nand_4_out, nand_3_out, nand_2_out);
  nand nand_5 (nand_5_out, nand_3_out, not_1_out);
  nand nand_6 (nand_6_out, not_1_out, nand_4_out);
  nand nand_7 (nand_7_out, nand_8_out, nand_6_out);
  nand nand_8 (nand_8_out, nand_5_out, nand_7_out);
  LED Q0 (.in(nand_8_out));
  LED nQ0 (.in(nand_7_out));
  not not_2 (not_2_out, clk);
  nand nand_9 (nand_9_out, clk, nand_16_out, nand_8_out);
  nand nand_10 (nand_10_out, nand_7_out, nand_15_out, clk);
  nand nand_11 (nand_11_out, nand_9_out, nand_12_out);
  nand nand_12 (nand_12_out, nand_11_out, nand_10_out);
  LED Q2 (.in(nand_8_out));
  LED Q3 (.in(nand_15_out));
  nand nand_13 (nand_13_out, nand_11_out, not_2_out);
  nand nand_14 (nand_14_out, not_2_out, nand_12_out);
  LED Q5 (.in(nand_23_out));
  nand nand_15 (nand_15_out, nand_13_out, nand_16_out);
  nand nand_16 (nand_16_out, nand_15_out, nand_14_out);
  LED Q1 (.in(nand_15_out));
  LED nQ1 (.in(nand_16_out));
  not not_3 (not_3_out, clk);
  nand nand_17 (nand_17_out, clk, nand_24_out, nand_15_out);
  nand nand_18 (nand_18_out, nand_16_out, nand_23_out, clk);
  nand nand_19 (nand_19_out, nand_17_out, nand_20_out);
  nand nand_20 (nand_20_out, nand_19_out, nand_18_out);
  nand nand_21 (nand_21_out, nand_19_out, not_3_out);
  nand nand_22 (nand_22_out, not_3_out, nand_20_out);
  nand nand_23 (nand_23_out, nand_21_out, nand_24_out);
  nand nand_24 (nand_24_out, nand_23_out, nand_22_out);
  LED Q4 (.in(nand_23_out));
  LED nQ2 (.in(nand_24_out));
endmodule
