// Digital circuit ldPC0_bit.dig as structural Verilog
module ldPC0_bit (
  input  CLR,
  input  D0_a,
  input  CCNT_e,
  input  ncnt__LD,
  input  KSCD,
  input  CLK,
  output Q,
  output nQ
);

  wire and_1_out, and_2_out, and_3_out, not_1_out, not_2_out, or_1_out;

  not not_1 (not_1_out, D0_a);
  not not_2 (not_2_out, ncnt__LD);
  and and_1 (and_1_out, not_1_out, ncnt__LD);
  and and_2 (and_2_out, D0_a, ncnt__LD);
  and and_3 (and_3_out, CCNT_e, KSCD, not_2_out);
  or or_1 (or_1_out, and_1_out, CLR);
  JK_FF_AS jk_ff_as_1 (.Set(and_2_out), .J(and_3_out), .C(CLK), .K(and_3_out), .Clr(or_1_out), .Q(Q), .nQ(nQ));

  // Notes on the sheet:
  //   CCNT_e: default 1
  //   KSCD: default 1
endmodule
