// Digital circuit sap1con.dig as structural Verilog
module sap1con (
  input  Cp,
  input  Ep,
  input  nLm,
  input  nCe,
  input  nL1,
  input  nE1,
  input  nLa,
  input  Ea,
  input  Su,
  input  Eu,
  input  nLb,
  input  nLo
);
endmodule
