// Digital circuit sap1pc.dig as structural Verilog
module sap1pc (
  input  CLR,
  input  Cp,
  input  nClk,
  input  Ep,
  input  clk,
  input  CLR_2,
  input  Ep_2,
  input  Re_a,
  input  in_17,
  output AI0,
  output AI1,
  output AI2,
  output AI3,
  output AI4,
  output AI5,
  output AI6,
  output AI7
);

  wire and_1_out, and_2_out, and_3_out, and_4_out, PR_out, pullup_2_out;
  wire [3:0] d_ff_as_1_q, jk_ff_as_1_q;
  wire [7:4] pullup_1_out;

  DipSwitch PR (.out(PR_out));
  and and_1 (and_1_out, Re_a, clk);
  JK_FF_AS jk_ff_as_1 (.Set(PR_out), .J(Cp), .C(clk), .K(Cp), .Clr(CLR), .Q(jk_ff_as_1_q[0]));  // open: nQ
  and and_2 (and_2_out, Cp, jk_ff_as_1_q[0]);
  assign AI0 = Ep ? jk_ff_as_1_q[0] : 1'bz;  // Driver driver_1
  JK_FF_AS jk_ff_as_2 (
    .Set(PR_out), .J(and_2_out), .C(clk), .K(and_2_out), .Clr(CLR), .Q(jk_ff_as_1_q[1]));  // open: nQ
  D_FF_AS d_ff_as_1 (.Set(in_17), .D(AI0), .C(and_1_out), .Clr(CLR_2), .Q(d_ff_as_1_q[0]));  // open: nQ
  and and_3 (and_3_out, Cp, and_2_out, jk_ff_as_1_q[1]);
  assign AI1 = Ep ? jk_ff_as_1_q[1] : 1'bz;  // Driver driver_2
  assign AI4 = Ep_2 ? d_ff_as_1_q[0] : 1'bz;  // Driver driver_3
  JK_FF_AS jk_ff_as_3 (
    .Set(PR_out), .J(and_3_out), .C(clk), .K(and_3_out), .Clr(CLR), .Q(jk_ff_as_1_q[2]));  // open: nQ
  D_FF_AS d_ff_as_2 (.Set(in_17), .D(AI1), .C(and_1_out), .Clr(CLR_2), .Q(d_ff_as_1_q[1]));  // open: nQ
  and and_4 (and_4_out, Cp, and_3_out, jk_ff_as_1_q[2]);
  assign AI2 = Ep ? jk_ff_as_1_q[2] : 1'bz;  // Driver driver_4
  assign AI5 = Ep_2 ? d_ff_as_1_q[1] : 1'bz;  // Driver driver_5
  JK_FF_AS jk_ff_as_4 (
    .Set(PR_out), .J(and_4_out), .C(clk), .K(and_4_out), .Clr(CLR), .Q(jk_ff_as_1_q[3]));  // open: nQ
  D_FF_AS d_ff_as_3 (.Set(in_17), .D(AI2), .C(and_1_out), .Clr(CLR_2), .Q(d_ff_as_1_q[2]));  // open: nQ
  assign AI6 = Ep_2 ? d_ff_as_1_q[2] : 1'bz;  // Driver driver_6
  assign AI3 = Ep ? jk_ff_as_1_q[3] : 1'bz;  // Driver driver_7
  D_FF_AS d_ff_as_4 (.Set(in_17), .D(AI3), .C(and_1_out), .Clr(CLR_2), .Q(d_ff_as_1_q[3]));  // open: nQ
  assign AI7 = Ep_2 ? d_ff_as_1_q[3] : 1'bz;  // Driver driver_8
  Seven_Seg_Hex seven_seg_hex_1 (.d(jk_ff_as_1_q), .dp(clk));
  PullUp #(.Bits(4)) pullup_1 (.out(pullup_1_out));
  Seven_Seg_Hex seven_seg_hex_2 (.d(d_ff_as_1_q), .dp(pullup_2_out));
  PullUp pullup_2 (.out(pullup_2_out));
endmodule
