// Digital circuit sapALU0.dig as structural Verilog
module sapALU0 (
  input  CY_in,
  input  A,
  input  B,
  input  SUB,
  input  nINV,
  output S,
  output CY_ou,
  output SB_in
);

  wire and_1_out, and_2_out, and_3_out, and_4_out, not_1_out, xor_2_out, xor_3_out;

  not not_1 (not_1_out, nINV);
  xor xor_1 (SB_in, B, SUB);
  xor xor_2 (xor_2_out, A, not_1_out);
  and and_1 (and_1_out, CY_in, nINV);
  and and_2 (and_2_out, nINV, SB_in);
  xor xor_3 (xor_3_out, xor_2_out, and_2_out);
  xor xor_4 (S, and_1_out, xor_3_out);
  and and_3 (and_3_out, and_1_out, xor_3_out);
  and and_4 (and_4_out, xor_2_out, and_2_out);
  or or_1 (CY_ou, and_3_out, and_4_out);
endmodule

/* Test case SomadorA:
A B CY_in ~INV SUB  S CY_ou
0 0 0     1     0   0  0 
1 0 0     1     0   1  0 
0 1 0     1     0   1  0 
0 0 1     1     0   1  0 
1 0 1     1     0   0  1 
0 1 1     1     0   0  1 
1 1 1     1     0   1  1 
0 X X     0     0   1  0
1 X X     0     0   0  0
*/

/* Test case Subtracao:
A B SB_in CY_in ~INV SUB  S CY_ou
0 0   1     0     1   1   1  0 
1 0   1     0     1   1   0  1 
0 1   0     0     1   1   0  0 
0 0   1     1     1   1   0  1 
1 0   1     1     1   1   1  1 
0 1   0     1     1   1   1  0 
1 1   0     1     1   1   0  1 
0 X   X     X     0   1   1  0
1 X   X     X     0   1   0  0
*/
