// Digital circuit sapRegX.dig as structural Verilog
module sapRegX (
  input  E_in,
  input  [7:0] D_x,
  input  E_out,
  output [7:0] Q_x
);

  DffwEna dffwena_1 (.D(D_x[0]), .E_in(E_in), .Q(Q_x[0]), .E_out(E_out));
  DffwEna dffwena_2 (.D(D_x[1]), .E_in(E_in), .Q(Q_x[1]), .E_out(E_out));
  DffwEna dffwena_3 (.D(D_x[2]), .E_in(E_in), .Q(Q_x[2]), .E_out(E_out));
  DffwEna dffwena_4 (.D(D_x[3]), .E_in(E_in), .Q(Q_x[3]), .E_out(E_out));
  DffwEna dffwena_5 (.D(D_x[4]), .E_in(E_in), .Q(Q_x[4]), .E_out(E_out));
  DffwEna dffwena_6 (.D(D_x[5]), .E_in(E_in), .Q(Q_x[5]), .E_out(E_out));
  DffwEna dffwena_7 (.D(D_x[6]), .E_in(E_in), .Q(Q_x[6]), .E_out(E_out));
  DffwEna dffwena_8 (.D(D_x[7]), .E_in(E_in), .Q(Q_x[7]), .E_out(E_out));
endmodule
