// Digital circuit sem0.dig as structural Verilog
module sem0 (
  input  clk
);

  wire and_1_out, and_2_out, and_3_out, and_4_out, and_5_out, and_6_out, not_1_out, not_2_out, not_3_out,
       or_1_out, or_2_out;
  wire [1:0] counter_1_out;
  wire [2:2] counter_1_out_2;

  Seven_Seg_Hex seven_seg_hex_1 (.d({1'b0, counter_1_out_2[2], counter_1_out}), .dp(1'b0));
  Counter #(.Bits(3)) counter_1 (
    .en(1'b1), .C(clk), .clr(1'b0), .out({counter_1_out_2[2], counter_1_out}));  // open: ovf
  Seven_Seg_Hex seven_seg_hex_2 (.d({2'b00, counter_1_out}), .dp(1'b0));
  not not_1 (not_1_out, counter_1_out_2[2]);
  not not_2 (not_2_out, counter_1_out[0]);
  not not_3 (not_3_out, counter_1_out[1]);
  LED Ta (.in(not_1_out));
  and and_1 (and_1_out, counter_1_out[1], not_1_out);
  and and_2 (and_2_out, counter_1_out[0], not_3_out, not_1_out);
  and and_3 (and_3_out, not_2_out, not_3_out, not_1_out);
  or or_1 (or_1_out, counter_1_out_2[2], and_1_out);
  LED AVm (.in(or_1_out));
  LED Aam (.in(and_2_out));
  LED Avd (.in(and_3_out));
  and and_4 (and_4_out, counter_1_out[1], counter_1_out_2[2]);
  and and_5 (and_5_out, counter_1_out[0], not_3_out, counter_1_out_2[2]);
  and and_6 (and_6_out, not_2_out, not_3_out, counter_1_out_2[2]);
  or or_2 (or_2_out, not_1_out, and_4_out);
  LED BVM (.in(or_2_out));
  LED Bam (.in(and_5_out));
  LED Bvd (.in(and_6_out));
endmodule
